// Logisim project kalkulu.circ as structural Verilog: 5 circuits, main circuit main
module main (
  input  IN1,
  input  in_2,
  input  in_3,
  input  in_4,
  input  IN2,
  input  in_6,
  input  in_7,
  input  in_8
);

  wire clock_1_out, decoder_module_1__0000, decoder_module_1__0001, decoder_module_1__0010,
       decoder_module_1__0011, decoder_module_1__0100, decoder_module_1__0101, decoder_module_1__0110,
       decoder_module_1__0111, decoder_module_1__1000, decoder_module_1__1001, decoder_module_1__1010,
       decoder_module_1__1011, decoder_module_1__1100, decoder_module_1__1101, decoder_module_1__1110,
       decoder_module_1__1111, undriven, undriven_2, undriven_3, undriven_4;

  Clock #(.highDuration(1), .lowDuration(1)) clock_1 (.out(clock_1_out));
  decoder_module decoder_module_1 (
    .CLOCK(clock_1_out), ._1XXX__MSB(undriven), .X1XX(undriven_2), .XX1X(undriven_3), .XXX1__LSB(undriven_4),
    ._0000(decoder_module_1__0000), ._0001(decoder_module_1__0001), ._0010(decoder_module_1__0010),
    ._0011(decoder_module_1__0011), ._0100(decoder_module_1__0100), ._0101(decoder_module_1__0101),
    ._0110(decoder_module_1__0110), ._0111(decoder_module_1__0111), ._1000(decoder_module_1__1000),
    ._1001(decoder_module_1__1001), ._1010(decoder_module_1__1010), ._1011(decoder_module_1__1011),
    ._1100(decoder_module_1__1100), ._1101(decoder_module_1__1101), ._1110(decoder_module_1__1110),
    ._1111(decoder_module_1__1111));
  quad_pulse_triggered_D_flip_flop quad_pulse_triggered_d_flip_flop_1 (
    .D1(IN1), .D2(in_2), .D3(in_3), .D4(in_4), .Clock(clock_1_out));  // open: Q1, Q2, Q3, Q4
  quad_pulse_triggered_D_flip_flop quad_pulse_triggered_d_flip_flop_2 (
    .D1(IN2), .D2(in_6), .D3(in_7), .D4(in_8), .Clock(clock_1_out));  // open: Q1, Q2, Q3, Q4

  // Notes on the sheet:
  //   Decoder Module
  //   -> 0000
  //   -> 1111
endmodule

module gated_D_latch (
  input  D,
  input  E,
  output Q,
  output Q_not
);

  wire nand_1_out, nand_2_out;

  nand nand_1 (nand_1_out, D, E);
  nand nand_2 (nand_2_out, nand_1_out, E);
  nand nand_3 (Q, nand_1_out, Q_not);
  nand nand_4 (Q_not, Q, nand_2_out);
endmodule

module pulse_triggered_D_flip_flop (
  input  D,
  input  Clock,
  output Q,
  output Q_not
);

  wire gated_d_latch_1_q, not_1_out;

  gated_D_latch gated_d_latch_1 (.D(D), .E(Clock), .Q(gated_d_latch_1_q));  // open: Q_not
  not not_1 (not_1_out, Clock);
  gated_D_latch gated_d_latch_2 (.D(gated_d_latch_1_q), .E(not_1_out), .Q(Q), .Q_not(Q_not));
endmodule

module quad_pulse_triggered_D_flip_flop (
  input  Clock,
  input  D1,
  input  D2,
  input  D3,
  input  D4,
  output Q1,
  output Q2,
  output Q3,
  output Q4
);

  pulse_triggered_D_flip_flop pulse_triggered_d_flip_flop_1 (.D(D1), .Clock(Clock), .Q(Q1));  // open: Q_not
  pulse_triggered_D_flip_flop pulse_triggered_d_flip_flop_2 (.D(D2), .Clock(Clock), .Q(Q2));  // open: Q_not
  pulse_triggered_D_flip_flop pulse_triggered_d_flip_flop_3 (.D(D3), .Clock(Clock), .Q(Q3));  // open: Q_not
  pulse_triggered_D_flip_flop pulse_triggered_d_flip_flop_4 (.D(D4), .Clock(Clock), .Q(Q4));  // open: Q_not
endmodule

module decoder_module (
  input  CLOCK,
  input  _1XXX__MSB,
  input  X1XX,
  input  XX1X,
  input  XXX1__LSB,
  output _0000,
  output _0001,
  output _0010,
  output _0011,
  output _0100,
  output _0101,
  output _0110,
  output _0111,
  output _1000,
  output _1001,
  output _1010,
  output _1011,
  output _1100,
  output _1101,
  output _1110,
  output _1111
);

  wire and_1_out, and_2_out, and_3_out, and_4_out, and_5_out, and_6_out, and_7_out, and_8_out, not_1_out,
       not_2_out, not_3_out, not_4_out, quad_pulse_triggered_d_flip_flop_1_q1,
       quad_pulse_triggered_d_flip_flop_1_q2, quad_pulse_triggered_d_flip_flop_1_q3,
       quad_pulse_triggered_d_flip_flop_1_q4;

  not not_1 (not_1_out, quad_pulse_triggered_d_flip_flop_1_q1);
  quad_pulse_triggered_D_flip_flop quad_pulse_triggered_d_flip_flop_1 (
    .D1(_1XXX__MSB), .D2(X1XX), .D3(XX1X), .D4(XXX1__LSB), .Clock(CLOCK),
    .Q1(quad_pulse_triggered_d_flip_flop_1_q1), .Q2(quad_pulse_triggered_d_flip_flop_1_q2),
    .Q3(quad_pulse_triggered_d_flip_flop_1_q3), .Q4(quad_pulse_triggered_d_flip_flop_1_q4));
  not not_2 (not_2_out, quad_pulse_triggered_d_flip_flop_1_q2);
  not not_3 (not_3_out, quad_pulse_triggered_d_flip_flop_1_q3);
  not not_4 (not_4_out, quad_pulse_triggered_d_flip_flop_1_q4);
  and and_1 (and_1_out, not_1_out, not_2_out);
  and and_2 (and_2_out, not_1_out, quad_pulse_triggered_d_flip_flop_1_q2);
  and and_3 (and_3_out, quad_pulse_triggered_d_flip_flop_1_q1, not_2_out);
  and and_4 (and_4_out, quad_pulse_triggered_d_flip_flop_1_q1, quad_pulse_triggered_d_flip_flop_1_q2);
  and and_5 (and_5_out, not_4_out, not_3_out);
  and and_6 (and_6_out, quad_pulse_triggered_d_flip_flop_1_q4, not_3_out);
  and and_7 (and_7_out, quad_pulse_triggered_d_flip_flop_1_q3, not_4_out);
  and and_8 (and_8_out, quad_pulse_triggered_d_flip_flop_1_q3, quad_pulse_triggered_d_flip_flop_1_q4);
  and and_9 (_0000, and_1_out, and_5_out);
  and and_10 (_0001, and_1_out, and_6_out);
  and and_11 (_0010, and_1_out, and_7_out);
  and and_12 (_0011, and_1_out, and_8_out);
  and and_13 (_0100, and_2_out, and_5_out);
  and and_14 (_0101, and_2_out, and_6_out);
  and and_15 (_0110, and_2_out, and_7_out);
  and and_16 (_0111, and_2_out, and_8_out);
  and and_17 (_1000, and_3_out, and_5_out);
  and and_18 (_1001, and_3_out, and_6_out);
  and and_19 (_1010, and_3_out, and_7_out);
  and and_20 (_1011, and_3_out, and_8_out);
  and and_21 (_1100, and_4_out, and_5_out);
  and and_22 (_1101, and_4_out, and_6_out);
  and and_23 (_1110, and_4_out, and_7_out);
  and and_24 (_1111, and_4_out, and_8_out);

  // Notes on the sheet:
  //   00XX
  //   01XX
  //   10XX
  //   11XX
  //   XX00
  //   XX01
  //   XX10
  //   XX11
endmodule
