// Logisim project kalkulu.circ as structural Verilog
module decoder (
  input  _1XXX,
  input  X1XX,
  input  XX1X,
  input  XXX1,
  output _0000,
  output _0001,
  output _0010,
  output _0011,
  output _0100,
  output _0101,
  output _0110,
  output _0111,
  output _1000,
  output _1001,
  output _1010,
  output _1011,
  output _1100,
  output _1101,
  output _1110,
  output _1111
);

  wire and_1_out, and_2_out, and_3_out, and_4_out, and_5_out, and_6_out, and_7_out, and_8_out, not_1_out,
       not_2_out, not_3_out, not_4_out;

  not not_1 (not_1_out, _1XXX);
  not not_2 (not_2_out, X1XX);
  not not_3 (not_3_out, XX1X);
  not not_4 (not_4_out, XXX1);
  and and_1 (and_1_out, not_1_out, not_2_out);
  and and_2 (and_2_out, not_1_out, X1XX);
  and and_3 (and_3_out, _1XXX, not_2_out);
  and and_4 (and_4_out, _1XXX, X1XX);
  and and_5 (and_5_out, not_3_out, not_4_out);
  and and_6 (and_6_out, not_3_out, XXX1);
  and and_7 (and_7_out, XX1X, not_4_out);
  and and_8 (and_8_out, XX1X, XXX1);
  and and_9 (_0000, and_1_out, and_5_out);
  and and_10 (_0001, and_1_out, and_6_out);
  and and_11 (_0010, and_1_out, and_7_out);
  and and_12 (_0011, and_1_out, and_8_out);
  and and_13 (_0100, and_2_out, and_5_out);
  and and_14 (_0101, and_2_out, and_6_out);
  and and_15 (_0110, and_2_out, and_7_out);
  and and_16 (_0111, and_2_out, and_8_out);
  and and_17 (_1000, and_3_out, and_5_out);
  and and_18 (_1001, and_3_out, and_6_out);
  and and_19 (_1010, and_3_out, and_7_out);
  and and_20 (_1011, and_3_out, and_8_out);
  and and_21 (_1100, and_4_out, and_5_out);
  and and_22 (_1101, and_4_out, and_6_out);
  and and_23 (_1110, and_4_out, and_7_out);
  and and_24 (_1111, and_4_out, and_8_out);

  // Notes on the sheet:
  //   01XX
  //   00XX
  //   10XX
  //   11XX
  //   XX00
  //   XX01
  //   XX10
  //   XX11
endmodule
